// Logisim project arcanoid.circ as structural Verilog: 14 circuits, main circuit main
module main (
);

  wire clk, kinematic_controller_1_rst_2, rst, video_scheme_1_rst_2, video_scheme_2_rst_2,
       video_scheme_3_rst_2;
  wire [3:0] divisor_by_10_1_score_low, divisor_by_10_1_score_up, joystick_1_x;
  wire [4:0] control_bat_1_output_x_bat, kinematic_controller_1_ballx, kinematic_controller_1_bally,
       kinematic_controller_1_chip_id, kinematic_controller_1_x_joystick_out, video_scheme_1_chip_id_out,
       video_scheme_1_x_ball_out, video_scheme_1_x_bat_out, video_scheme_1_y_ball_out,
       video_scheme_2_chip_id_out, video_scheme_2_x_ball_out, video_scheme_2_x_bat_out,
       video_scheme_2_y_ball_out, video_scheme_3_chip_id_out, video_scheme_3_x_ball_out,
       video_scheme_3_x_bat_out, video_scheme_3_y_ball_out;
  wire [7:0] score;
  wire [7:4] divisor_by_10_1_score_low_2, divisor_by_10_1_score_up_2;
  wire [31:0] video_scheme_1_out_6, video_scheme_1_out_7, video_scheme_1_out_8, video_scheme_1_out_9,
       video_scheme_1_out_10, video_scheme_1_out_11, video_scheme_1_out_12, video_scheme_1_out_13,
       video_scheme_2_out_6, video_scheme_2_out_7, video_scheme_2_out_8, video_scheme_2_out_9,
       video_scheme_2_out_10, video_scheme_2_out_11, video_scheme_2_out_12, video_scheme_2_out_13,
       video_scheme_3_out_6, video_scheme_3_out_7, video_scheme_3_out_8, video_scheme_3_out_9,
       video_scheme_3_out_10, video_scheme_3_out_11, video_scheme_3_out_12, video_scheme_3_out_13,
       video_scheme_4_out_6, video_scheme_4_out_7, video_scheme_4_out_8, video_scheme_4_out_9,
       video_scheme_4_out_10, video_scheme_4_out_11, video_scheme_4_out_12, video_scheme_4_out_13;

  Joystick joystick_1 (.x(joystick_1_x));  // open: y
  Clock clock_1 (.out(clk));
  Button button_1 (.out(rst));
  control_bat control_bat_1 (
    .gamepad_input(joystick_1_x), .clock(clk), .output_x_bat(control_bat_1_output_x_bat), .restart(rst));
  DotMatrix #(.inputtype("row"), .matrixcols(32), .matrixrows(32)) dotmatrix_1 (
    .row0(video_scheme_1_out_10), .row1(video_scheme_1_out_6), .row2(video_scheme_1_out_11),
    .row3(video_scheme_1_out_7), .row4(video_scheme_1_out_12), .row5(video_scheme_1_out_8),
    .row6(video_scheme_1_out_13), .row7(video_scheme_1_out_9), .row8(video_scheme_2_out_10),
    .row9(video_scheme_2_out_6), .row10(video_scheme_2_out_11), .row11(video_scheme_2_out_7),
    .row12(video_scheme_2_out_12), .row13(video_scheme_2_out_8), .row14(video_scheme_2_out_13),
    .row15(video_scheme_2_out_9), .row16(video_scheme_3_out_10), .row17(video_scheme_3_out_6),
    .row18(video_scheme_3_out_11), .row19(video_scheme_3_out_7), .row20(video_scheme_3_out_12),
    .row21(video_scheme_3_out_8), .row22(video_scheme_3_out_13), .row23(video_scheme_3_out_9),
    .row24(video_scheme_4_out_10), .row25(video_scheme_4_out_6), .row26(video_scheme_4_out_11),
    .row27(video_scheme_4_out_7), .row28(video_scheme_4_out_12), .row29(video_scheme_4_out_8),
    .row30(video_scheme_4_out_13), .row31(video_scheme_4_out_9));
  video_scheme video_scheme_1 (
    .chip_ID(kinematic_controller_1_chip_id), .x_ball(kinematic_controller_1_ballx),
    .y_ball(kinematic_controller_1_bally), .x_bat(kinematic_controller_1_x_joystick_out),
    .chip_ID_out(video_scheme_1_chip_id_out), .x_ball_out(video_scheme_1_x_ball_out),
    .y_ball_out(video_scheme_1_y_ball_out), .x_bat_out(video_scheme_1_x_bat_out),
    .out_10(video_scheme_1_out_10), .out_6(video_scheme_1_out_6), .out_11(video_scheme_1_out_11),
    .out_7(video_scheme_1_out_7), .out_12(video_scheme_1_out_12), .out_8(video_scheme_1_out_8),
    .out_13(video_scheme_1_out_13), .out_9(video_scheme_1_out_9), .rst(kinematic_controller_1_rst_2),
    .rst_2(video_scheme_1_rst_2));
  video_scheme video_scheme_2 (
    .chip_ID(video_scheme_1_chip_id_out), .x_ball(video_scheme_1_x_ball_out),
    .y_ball(video_scheme_1_y_ball_out), .x_bat(video_scheme_1_x_bat_out),
    .chip_ID_out(video_scheme_2_chip_id_out), .x_ball_out(video_scheme_2_x_ball_out),
    .y_ball_out(video_scheme_2_y_ball_out), .x_bat_out(video_scheme_2_x_bat_out),
    .out_10(video_scheme_2_out_10), .out_6(video_scheme_2_out_6), .out_11(video_scheme_2_out_11),
    .out_7(video_scheme_2_out_7), .out_12(video_scheme_2_out_12), .out_8(video_scheme_2_out_8),
    .out_13(video_scheme_2_out_13), .out_9(video_scheme_2_out_9), .rst(video_scheme_1_rst_2),
    .rst_2(video_scheme_2_rst_2));
  video_scheme video_scheme_3 (
    .chip_ID(video_scheme_2_chip_id_out), .x_ball(video_scheme_2_x_ball_out),
    .y_ball(video_scheme_2_y_ball_out), .x_bat(video_scheme_2_x_bat_out),
    .chip_ID_out(video_scheme_3_chip_id_out), .x_ball_out(video_scheme_3_x_ball_out),
    .y_ball_out(video_scheme_3_y_ball_out), .x_bat_out(video_scheme_3_x_bat_out),
    .out_10(video_scheme_3_out_10), .out_6(video_scheme_3_out_6), .out_11(video_scheme_3_out_11),
    .out_7(video_scheme_3_out_7), .out_12(video_scheme_3_out_12), .out_8(video_scheme_3_out_8),
    .out_13(video_scheme_3_out_13), .out_9(video_scheme_3_out_9), .rst(video_scheme_2_rst_2),
    .rst_2(video_scheme_3_rst_2));
  video_scheme video_scheme_4 (
    .chip_ID(video_scheme_3_chip_id_out), .x_ball(video_scheme_3_x_ball_out),
    .y_ball(video_scheme_3_y_ball_out), .x_bat(video_scheme_3_x_bat_out), .out_10(video_scheme_4_out_10),
    .out_6(video_scheme_4_out_6), .out_11(video_scheme_4_out_11), .out_7(video_scheme_4_out_7),
    .out_12(video_scheme_4_out_12), .out_8(video_scheme_4_out_8), .out_13(video_scheme_4_out_13),
    .out_9(video_scheme_4_out_9), .rst(video_scheme_3_rst_2));  // open: chip_ID_out, x_ball_out, y_ball_out, x_bat_out, rst_2
  kinematic_controller kinematic_controller_1 (
    .clock(clk), .x_joystick(control_bat_1_output_x_bat), .ballx(kinematic_controller_1_ballx),
    .bally(kinematic_controller_1_bally), .x_joystick_out(kinematic_controller_1_x_joystick_out),
    .score(score), .chip_ID(kinematic_controller_1_chip_id), .rst(rst), .rst_2(kinematic_controller_1_rst_2));
  Hex_Digit_Display hex_digit_display_1 (.value(divisor_by_10_1_score_up));  // open: dp
  Hex_Digit_Display hex_digit_display_2 (.value(divisor_by_10_1_score_low));  // open: dp
  divisor_by_10 divisor_by_10_1 (
    .data(score), .score_up({divisor_by_10_1_score_up_2, divisor_by_10_1_score_up}),
    .score_low({divisor_by_10_1_score_low_2, divisor_by_10_1_score_low}));
endmodule

module control_bat (
  input  restart,
  input  [3:0] gamepad_input,
  input  clock,
  output [4:0] output_x_bat
);

  wire and_1_out, and_2_out, comparator_1_eq, comparator_1_lt, comparator_2_eq, comparator_3_eq,
       counter_1_carry, not_1_out, not_2_out, not_3_out, not_4_out, or_1_out;
  wire [4:0] counter_2_q;

  Counter #(.width(5), .max('h1f)) counter_1 (
    .count(clock), .carry(counter_1_carry), .clk(clock));  // open: load, D, Q, clr
  not not_1 (not_1_out, comparator_1_eq);
  and and_1 (and_1_out, comparator_2_eq, not_1_out, not_2_out);
  not not_2 (not_2_out, comparator_1_lt);
  and and_2 (and_2_out, comparator_3_eq, not_3_out, comparator_1_lt);
  not not_3 (not_3_out, comparator_1_eq);
  Comparator #(.width(4), .mode("unsigned")) comparator_1 (
    .a(gamepad_input), .b(4'b1000), .eq(comparator_1_eq), .lt(comparator_1_lt));  // open: gt
  or or_1 (or_1_out, comparator_1_eq, and_1_out, and_2_out);
  Counter #(.width(5), .max('h1f)) counter_2 (
    .load(comparator_1_lt), .D(5'b10001), .count(not_4_out), .Q(counter_2_q), .clk(counter_1_carry),
    .clr(restart));  // open: carry
  not not_4 (not_4_out, or_1_out);
  Adder #(.width(5)) adder_1 (.a(5'b10001), .b(counter_2_q), .out(output_x_bat));  // open: cin, cout
  Comparator #(.width(5), .mode("unsigned")) comparator_2 (
    .a(output_x_bat), .b({5{1'b1}}), .eq(comparator_2_eq));  // open: gt, lt
  Comparator #(.width(5), .mode("unsigned")) comparator_3 (
    .a(output_x_bat), .b(5'b00010), .eq(comparator_3_eq));  // open: gt, lt

  // Other names for the same wires on the sheet: rst = restart
endmodule

module video_chip (
  input  [4:0] chip_ID,
  input  [4:0] x_ball,
  input  [4:0] y_ball,
  input  [4:0] x_bat,
  input  rst,
  output [4:0] chip_ID_out,
  output [31:0] out,
  output [4:0] x_ball_out,
  output [4:0] y_ball_out,
  output [4:0] y_bat_out,
  output rst_2
);

  wire [31:0] decoder_32_inv_1_out, decoder_32_inv_2_out, shifter_1_out, shifter_2_out;

  Adder #(.width(5)) adder_1 (.a(5'b00001), .b(chip_ID), .out(chip_ID_out));  // open: cin, cout
  decoder_32_inv decoder_32_inv_1 (.data(x_ball), .A(y_ball), .B(chip_ID), .out(decoder_32_inv_1_out));
  decoder_32_inv decoder_32_inv_2 (.data(x_bat), .A(chip_ID), .B(5'b11101), .out(decoder_32_inv_2_out));
  Shifter #(.width(32)) shifter_1 (.in(decoder_32_inv_2_out), .\dist (5'b00010), .out(shifter_1_out));
  Shifter #(.width(32)) shifter_2 (.in(decoder_32_inv_2_out), .\dist (5'b00001), .out(shifter_2_out));
  assign out = decoder_32_inv_1_out | decoder_32_inv_2_out | shifter_1_out | shifter_2_out;  // OR_Gate or_1, 32 bits wide

  assign rst_2 = rst;
  assign x_ball_out = x_ball;
  assign y_ball_out = y_ball;
  assign y_bat_out = x_bat;
endmodule

module inrange (
  input  [4:0] xball,
  input  [4:0] xbat,
  output shareArow
);

  wire comparator_1_eq, comparator_2_eq, comparator_3_eq;
  wire [4:0] adder_1_out, adder_2_out;

  Comparator #(.width(5)) comparator_1 (.a(xball), .b(xbat), .eq(comparator_1_eq));  // open: gt, lt
  Adder #(.width(5)) adder_1 (.a(xbat), .b(5'b00001), .out(adder_1_out));  // open: cin, cout
  Comparator #(.width(5)) comparator_2 (.a(xball), .b(adder_2_out), .eq(comparator_2_eq));  // open: gt, lt
  Adder #(.width(5)) adder_2 (.a(xbat), .b(5'b00010), .out(adder_2_out));  // open: cin, cout
  Comparator #(.width(5)) comparator_3 (.a(xball), .b(adder_1_out), .eq(comparator_3_eq));  // open: gt, lt
  or or_1 (shareArow, comparator_1_eq, comparator_3_eq, comparator_2_eq);
endmodule

module reflect (
  input  [7:0] in_1,
  output [7:0] out_2
);

  wire comparator_1_eq;
  wire [7:0] adder_1_out, not_1_out;

  // Probe on in_1
  assign not_1_out = ~in_1;  // NOT_Gate not_1, 8 bits wide
  Adder adder_1 (.a(8'h1), .b(not_1_out), .out(adder_1_out));  // open: cin, cout
  Comparator comparator_1 (.a(in_1), .b(8'hfc), .eq(comparator_1_eq));  // open: gt, lt
  // Probe on out_2
  Multiplexer #(.width(8), .enable("false")) multiplexer_1 (
    .in0(adder_1_out), .in1(not_1_out), .out(out_2), .sel(comparator_1_eq));
endmodule

module kinematic_controller (
  input  clock,
  input  [4:0] x_joystick,
  input  rst,
  output [4:0] chip_ID,
  output [4:0] ballx,
  output [4:0] bally,
  output [4:0] x_joystick_out,
  output rst_2,
  output [7:0] score
);


  assign ballx = 5'b10000;
  assign bally = 5'b11100;
  assign chip_ID = {5{1'b0}};
  assign rst_2 = rst;
  assign score = 8'h56;
  assign x_joystick_out = x_joystick;

  // Other names for the same wires on the sheet: clk = clock
endmodule

module decoder_32 (
  input  [4:0] data,
  input  [4:0] A,
  input  [4:0] B,
  output [31:0] out
);

  wire comparator_1_eq;

  Comparator #(.width(5)) comparator_1 (.a(A), .b(B), .eq(comparator_1_eq));  // open: gt, lt
  Decoder #(.select(5), .disabled(0)) decoder_1 (
    .out0(out[0]), .out1(out[1]), .out2(out[2]), .out3(out[3]), .out4(out[4]), .out5(out[5]), .out6(out[6]),
    .out7(out[7]), .out8(out[8]), .out9(out[9]), .out10(out[10]), .out11(out[11]), .out12(out[12]),
    .out13(out[13]), .out14(out[14]), .out15(out[15]), .out16(out[16]), .out17(out[17]), .out18(out[18]),
    .out19(out[19]), .out20(out[20]), .out21(out[21]), .out22(out[22]), .out23(out[23]), .out24(out[24]),
    .out25(out[25]), .out26(out[26]), .out27(out[27]), .out28(out[28]), .out29(out[29]), .out30(out[30]),
    .out31(out[31]), .sel(data), .en(comparator_1_eq));
endmodule

module decoder_32_inv (
  input  [4:0] data,
  input  [4:0] A,
  input  [4:0] B,
  output [31:0] out
);

  wire comparator_1_eq;

  Comparator #(.width(5)) comparator_1 (.a(A), .b(B), .eq(comparator_1_eq));  // open: gt, lt
  Decoder #(.select(5), .disabled(0)) decoder_1 (
    .out0(out[31]), .out1(out[30]), .out2(out[29]), .out3(out[28]), .out4(out[27]), .out5(out[26]),
    .out6(out[25]), .out7(out[24]), .out8(out[23]), .out9(out[22]), .out10(out[21]), .out11(out[20]),
    .out12(out[19]), .out13(out[18]), .out14(out[17]), .out15(out[16]), .out16(out[15]), .out17(out[14]),
    .out18(out[13]), .out19(out[12]), .out20(out[11]), .out21(out[10]), .out22(out[9]), .out23(out[8]),
    .out24(out[7]), .out25(out[6]), .out26(out[5]), .out27(out[4]), .out28(out[3]), .out29(out[2]),
    .out30(out[1]), .out31(out[0]), .sel(data), .en(comparator_1_eq));
endmodule

module video_scheme (
  input  [4:0] chip_ID,
  input  [4:0] x_ball,
  input  [4:0] y_ball,
  input  [4:0] x_bat,
  input  rst,
  output [31:0] out_6,
  output [31:0] out_7,
  output [31:0] out_8,
  output [31:0] out_9,
  output [31:0] out_10,
  output [31:0] out_11,
  output [31:0] out_12,
  output [31:0] out_13,
  output [4:0] chip_ID_out,
  output [4:0] x_ball_out,
  output [4:0] y_ball_out,
  output [4:0] x_bat_out,
  output rst_2
);

  wire video_chip_1_rst_2, video_chip_2_rst_2, video_chip_3_rst_2, video_chip_4_rst_2, video_chip_5_rst_2,
       video_chip_6_rst_2, video_chip_7_rst_2;
  wire [4:0] video_chip_1_chip_id_out, video_chip_1_x_ball_out, video_chip_1_y_ball_out,
       video_chip_1_y_bat_out, video_chip_2_chip_id_out, video_chip_2_x_ball_out, video_chip_2_y_ball_out,
       video_chip_2_y_bat_out, video_chip_3_chip_id_out, video_chip_3_x_ball_out, video_chip_3_y_ball_out,
       video_chip_3_y_bat_out, video_chip_4_chip_id_out, video_chip_4_x_ball_out, video_chip_4_y_ball_out,
       video_chip_4_y_bat_out, video_chip_5_chip_id_out, video_chip_5_x_ball_out, video_chip_5_y_ball_out,
       video_chip_5_y_bat_out, video_chip_6_chip_id_out, video_chip_6_x_ball_out, video_chip_6_y_ball_out,
       video_chip_6_y_bat_out, video_chip_7_chip_id_out, video_chip_7_x_ball_out, video_chip_7_y_ball_out,
       video_chip_7_y_bat_out;

  video_chip video_chip_1 (
    .chip_ID(chip_ID), .x_ball(x_ball), .y_ball(y_ball), .x_bat(x_bat),
    .chip_ID_out(video_chip_1_chip_id_out), .out(out_10), .x_ball_out(video_chip_1_x_ball_out),
    .y_ball_out(video_chip_1_y_ball_out), .y_bat_out(video_chip_1_y_bat_out), .rst(rst),
    .rst_2(video_chip_1_rst_2));
  video_chip video_chip_2 (
    .chip_ID(video_chip_3_chip_id_out), .x_ball(video_chip_3_x_ball_out), .y_ball(video_chip_3_y_ball_out),
    .x_bat(video_chip_3_y_bat_out), .chip_ID_out(video_chip_2_chip_id_out), .out(out_11),
    .x_ball_out(video_chip_2_x_ball_out), .y_ball_out(video_chip_2_y_ball_out),
    .y_bat_out(video_chip_2_y_bat_out), .rst(video_chip_3_rst_2), .rst_2(video_chip_2_rst_2));
  video_chip video_chip_3 (
    .chip_ID(video_chip_1_chip_id_out), .x_ball(video_chip_1_x_ball_out), .y_ball(video_chip_1_y_ball_out),
    .x_bat(video_chip_1_y_bat_out), .chip_ID_out(video_chip_3_chip_id_out), .out(out_6),
    .x_ball_out(video_chip_3_x_ball_out), .y_ball_out(video_chip_3_y_ball_out),
    .y_bat_out(video_chip_3_y_bat_out), .rst(video_chip_1_rst_2), .rst_2(video_chip_3_rst_2));
  video_chip video_chip_4 (
    .chip_ID(video_chip_5_chip_id_out), .x_ball(video_chip_5_x_ball_out), .y_ball(video_chip_5_y_ball_out),
    .x_bat(video_chip_5_y_bat_out), .chip_ID_out(video_chip_4_chip_id_out), .out(out_12),
    .x_ball_out(video_chip_4_x_ball_out), .y_ball_out(video_chip_4_y_ball_out),
    .y_bat_out(video_chip_4_y_bat_out), .rst(video_chip_5_rst_2), .rst_2(video_chip_4_rst_2));
  video_chip video_chip_5 (
    .chip_ID(video_chip_2_chip_id_out), .x_ball(video_chip_2_x_ball_out), .y_ball(video_chip_2_y_ball_out),
    .x_bat(video_chip_2_y_bat_out), .chip_ID_out(video_chip_5_chip_id_out), .out(out_7),
    .x_ball_out(video_chip_5_x_ball_out), .y_ball_out(video_chip_5_y_ball_out),
    .y_bat_out(video_chip_5_y_bat_out), .rst(video_chip_2_rst_2), .rst_2(video_chip_5_rst_2));
  video_chip video_chip_6 (
    .chip_ID(video_chip_7_chip_id_out), .x_ball(video_chip_7_x_ball_out), .y_ball(video_chip_7_y_ball_out),
    .x_bat(video_chip_7_y_bat_out), .chip_ID_out(video_chip_6_chip_id_out), .out(out_13),
    .x_ball_out(video_chip_6_x_ball_out), .y_ball_out(video_chip_6_y_ball_out),
    .y_bat_out(video_chip_6_y_bat_out), .rst(video_chip_7_rst_2), .rst_2(video_chip_6_rst_2));
  video_chip video_chip_7 (
    .chip_ID(video_chip_4_chip_id_out), .x_ball(video_chip_4_x_ball_out), .y_ball(video_chip_4_y_ball_out),
    .x_bat(video_chip_4_y_bat_out), .chip_ID_out(video_chip_7_chip_id_out), .out(out_8),
    .x_ball_out(video_chip_7_x_ball_out), .y_ball_out(video_chip_7_y_ball_out),
    .y_bat_out(video_chip_7_y_bat_out), .rst(video_chip_4_rst_2), .rst_2(video_chip_7_rst_2));
  video_chip video_chip_8 (
    .chip_ID(video_chip_6_chip_id_out), .x_ball(video_chip_6_x_ball_out), .y_ball(video_chip_6_y_ball_out),
    .x_bat(video_chip_6_y_bat_out), .chip_ID_out(chip_ID_out), .out(out_9), .x_ball_out(x_ball_out),
    .y_ball_out(y_ball_out), .y_bat_out(x_bat_out), .rst(video_chip_6_rst_2), .rst_2(rst_2));
endmodule

module test (
  input  restart,
  input  clock,
  input  up,
  input  down,
  input  clock_2,
  input  left,
  input  right,
  output [4:0] output_x_bat,
  output [4:0] X,
  output [4:0] X_2
);

  wire and_1_out, and_2_out, comparator_1_eq, comparator_1_lt, comparator_2_eq, comparator_3_eq, not_1_out,
       not_2_out, not_3_out, not_4_out, or_1_out, or_2_out, or_3_out, or_4_out, or_5_out, or_6_out;
  wire [1:0] register_1_q, register_2_q;
  wire [3:0] undriven;
  wire [4:0] counter_1_q, dat;

  and and_1 (and_1_out, comparator_2_eq, not_1_out, not_2_out);
  not not_1 (not_1_out, comparator_1_eq);
  not not_2 (not_2_out, comparator_1_lt);
  not not_3 (not_3_out, comparator_1_eq);
  and and_2 (and_2_out, comparator_3_eq, not_3_out, comparator_1_lt);
  Comparator #(.width(4), .mode("unsigned")) comparator_1 (
    .a(undriven), .b(4'b1000), .eq(comparator_1_eq), .lt(comparator_1_lt));  // open: gt
  or or_1 (or_1_out, up, down);
  or or_2 (or_2_out, left, right);
  or or_3 (or_3_out, restart, comparator_1_lt);
  Counter #(.width(5), .max('h1f)) counter_1 (
    .load(or_3_out), .D(dat), .count(not_4_out), .Q(counter_1_q), .clk(clock));  // open: carry, clr
  not not_4 (not_4_out, or_4_out);
  or or_4 (or_4_out, comparator_1_eq, and_1_out, and_2_out);
  Transistor #(.\type ("n"), .width(5)) transistor_1 (.in(5'b10001), .out(dat), .gate(and_2_out));
  Pull_Resistor pull_resistor_1 (.node(dat));
  Register #(.width(2)) register_1 (.D({down, up}), .Q(register_1_q), .clk(or_1_out), .clr(or_2_out));  // open: en
  Register #(.width(2)) register_2 (.D({right, left}), .Q(register_2_q), .clk(or_2_out), .clr(or_1_out));  // open: en
  Adder #(.width(5)) adder_1 (.a(5'b10001), .b(counter_1_q), .out(output_x_bat));  // open: cin, cout
  Comparator #(.width(5), .mode("unsigned")) comparator_2 (
    .a(output_x_bat), .b({5{1'b1}}), .eq(comparator_2_eq));  // open: gt, lt
  Comparator #(.width(5), .mode("unsigned")) comparator_3 (
    .a(output_x_bat), .b(5'b00010), .eq(comparator_3_eq));  // open: gt, lt
  or or_5 (or_5_out, register_1_q[0], register_1_q[1]);
  or or_6 (or_6_out, register_2_q[0], register_2_q[1]);
  Counter #(.width(5), .max('h1f)) counter_2 (
    .load(register_1_q[1]), .count(or_5_out), .Q(X), .clk(clock_2));  // open: D, carry, clr
  Counter #(.width(5), .max('h14)) counter_3 (
    .load(register_2_q[1]), .count(or_6_out), .Q(X_2), .clk(clock_2));  // open: D, carry, clr

  // Other names for the same wires on the sheet: rst = restart
endmodule

module divisor_by_10 (
  input  [7:0] data,
  output [7:0] score_up,
  output [7:0] score_low
);

  Divider divider_1 (.a(data), .b(8'ha), .out(score_up), .rem(score_low));  // open: upper
endmodule

module blocks_detector (
  input  rst,
  input  [4:0] block_ID,
  input  [4:0] chip_ID
);

  wire and_1_out, and_2_out, and_3_out, and_4_out, and_5_out, and_6_out, and_7_out, and_8_out, and_9_out,
       and_10_out, and_11_out, and_12_out, and_13_out, and_14_out, and_15_out, and_16_out, and_17_out,
       and_18_out, and_19_out, and_20_out, and_21_out, and_22_out, and_23_out, and_24_out, comparator_1_gt,
       min_comparator_1_result, min_comparator_2_result, min_comparator_3_result, min_comparator_4_result,
       min_comparator_5_result, min_comparator_6_result, min_comparator_7_result, min_comparator_8_result,
       min_comparator_9_result, min_comparator_10_result, min_comparator_11_result, min_comparator_12_result,
       min_comparator_13_result, min_comparator_14_result, min_comparator_15_result,
       min_comparator_16_result, min_comparator_17_result, min_comparator_18_result,
       min_comparator_19_result, min_comparator_20_result, min_comparator_21_result,
       min_comparator_22_result, min_comparator_23_result, min_comparator_24_result;
  wire [1:0] transistor_1_out;
  wire [4:0] block_paint_1_shift_2, block_paint_3_shift_2, block_paint_5_shift_2, block_paint_7_shift_2,
       block_paint_9_shift_2, block_paint_11_shift_2, block_paint_13_shift_2, block_paint_15_shift_2,
       block_paint_17_shift_2, block_paint_19_shift_2, block_paint_21_shift_2, block_paint_23_shift_2,
       block_paint_25_shift_2, block_paint_27_shift_2, block_paint_29_shift_2, block_paint_31_shift_2,
       block_paint_33_shift_2, block_paint_35_shift_2, block_paint_37_shift_2, block_paint_39_shift_2,
       block_paint_41_shift_2, demultiplexer_1_out1, demultiplexer_1_out2, demultiplexer_1_out3,
       divider_1_out, divider_1_rem, min_comparator_1_first_2, min_comparator_1_second_2,
       min_comparator_2_first_2, min_comparator_2_second_2, min_comparator_3_first_2,
       min_comparator_3_second_2, min_comparator_4_first_2, min_comparator_4_second_2,
       min_comparator_5_first_2, min_comparator_5_second_2, min_comparator_6_first_2,
       min_comparator_6_second_2, min_comparator_7_first_2, min_comparator_7_second_2,
       min_comparator_8_first_2, min_comparator_8_second_2, min_comparator_9_first_2,
       min_comparator_9_second_2, min_comparator_10_first_2, min_comparator_10_second_2,
       min_comparator_11_first_2, min_comparator_11_second_2, min_comparator_12_first_2,
       min_comparator_12_second_2, min_comparator_13_first_2, min_comparator_13_second_2,
       min_comparator_14_first_2, min_comparator_14_second_2, min_comparator_15_first_2,
       min_comparator_15_second_2, min_comparator_16_first_2, min_comparator_16_second_2,
       min_comparator_17_first_2, min_comparator_17_second_2, min_comparator_18_first_2,
       min_comparator_18_second_2, min_comparator_19_first_2, min_comparator_19_second_2,
       min_comparator_20_first_2, min_comparator_20_second_2, min_comparator_21_first_2,
       min_comparator_21_second_2, or_1_out, pull_resistor_2_node, register_1_q, register_2_q, register_3_q,
       register_4_q, register_5_q, register_6_q, register_7_q, register_8_q, register_9_q, register_10_q,
       register_11_q, register_12_q, register_13_q, register_14_q, register_15_q, register_16_q,
       register_17_q, register_18_q, register_19_q, register_20_q, register_21_q, register_22_q,
       register_23_q, register_24_q;
  wire [4:2] transistor_1_out_2;

  Demultiplexer #(.select(2), .width(5)) demultiplexer_1 (
    .out1(demultiplexer_1_out1), .out2(demultiplexer_1_out2), .out3(demultiplexer_1_out3),
    .in(pull_resistor_2_node), .sel(transistor_1_out));  // open: out0, en
  Divider #(.width(5)) divider_1 (.a(block_ID), .b(5'b01000), .out(divider_1_out), .rem(divider_1_rem));  // open: upper
  assign or_1_out = divider_1_out | divider_1_rem;  // OR_Gate or_1, 5 bits wide
  Register #(.width(5)) register_1 (.Q(register_1_q), .clr(and_1_out));  // open: D, en, clk
  buf and_1 (and_1_out, min_comparator_1_result);  // AND_Gate
  min_comparator min_comparator_1 (
    .first(demultiplexer_1_out1), .second(5'b00001), .result(min_comparator_1_result),
    .second_2(min_comparator_1_second_2), .first_2(min_comparator_1_first_2));
  Register #(.width(5)) register_2 (.Q(register_2_q), .clr(and_2_out));  // open: D, en, clk
  buf and_2 (and_2_out, min_comparator_2_result);  // AND_Gate
  min_comparator min_comparator_2 (
    .first(demultiplexer_1_out2), .second(5'b00001), .result(min_comparator_2_result),
    .second_2(min_comparator_2_second_2), .first_2(min_comparator_2_first_2));
  Register #(.width(5)) register_3 (.Q(register_3_q), .clr(and_3_out));  // open: D, en, clk
  buf and_3 (and_3_out, min_comparator_3_result);  // AND_Gate
  min_comparator min_comparator_3 (
    .first(demultiplexer_1_out3), .second(5'b00001), .result(min_comparator_3_result),
    .second_2(min_comparator_3_second_2), .first_2(min_comparator_3_first_2));
  Comparator #(.width(5)) comparator_1 (.a(or_1_out), .b({5{1'b0}}), .gt(comparator_1_gt));  // open: eq, lt
  block_paint block_paint_1 (
    .data(register_1_q), .\string (5'b00001), .t_string(chip_ID), .shift(5'b00011),
    .shift_2(block_paint_1_shift_2));  // open: t_string_2
  block_paint block_paint_2 (
    .data(register_1_q), .\string (5'b00010), .t_string(chip_ID), .shift(5'b00011));  // open: shift_2, t_string_2
  block_paint block_paint_3 (
    .data(register_2_q), .\string (5'b00100), .shift(5'b00011), .shift_2(block_paint_3_shift_2));  // open: t_string, t_string_2
  block_paint block_paint_4 (
    .data(register_2_q), .\string (5'b00101), .shift(5'b00011));  // open: t_string, shift_2, t_string_2
  block_paint block_paint_5 (
    .data(register_3_q), .\string (5'b00111), .shift(5'b00011), .shift_2(block_paint_5_shift_2));  // open: t_string, t_string_2
  block_paint block_paint_6 (
    .data(register_3_q), .\string (5'b01000), .shift(5'b00011));  // open: t_string, shift_2, t_string_2
  Transistor #(.\type ("n"), .width(5)) transistor_1 (
    .in(divider_1_out), .out({transistor_1_out_2, transistor_1_out}), .gate(comparator_1_gt));
  Pull_Resistor pull_resistor_1 (.node({transistor_1_out_2, transistor_1_out}));
  Pull_Resistor pull_resistor_2 (.node(pull_resistor_2_node));
  Transistor #(.\type ("n"), .width(5)) transistor_2 (
    .in(divider_1_rem), .out(pull_resistor_2_node), .gate(comparator_1_gt));
  Register #(.width(5)) register_4 (.Q(register_4_q), .clr(and_4_out));  // open: D, en, clk
  buf and_4 (and_4_out, min_comparator_4_result);  // AND_Gate
  min_comparator min_comparator_4 (
    .first(min_comparator_1_first_2), .second(min_comparator_1_second_2), .result(min_comparator_4_result),
    .second_2(min_comparator_4_second_2), .first_2(min_comparator_4_first_2));
  Register #(.width(5)) register_5 (.Q(register_5_q), .clr(and_5_out));  // open: D, en, clk
  buf and_5 (and_5_out, min_comparator_5_result);  // AND_Gate
  min_comparator min_comparator_5 (
    .first(min_comparator_2_first_2), .second(min_comparator_2_second_2), .result(min_comparator_5_result),
    .second_2(min_comparator_5_second_2), .first_2(min_comparator_5_first_2));
  Register #(.width(5)) register_6 (.Q(register_6_q), .clr(and_6_out));  // open: D, en, clk
  buf and_6 (and_6_out, min_comparator_6_result);  // AND_Gate
  min_comparator min_comparator_6 (
    .first(min_comparator_3_first_2), .second(min_comparator_3_second_2), .result(min_comparator_6_result),
    .second_2(min_comparator_6_second_2), .first_2(min_comparator_6_first_2));
  block_paint block_paint_7 (
    .data(register_4_q), .\string (5'b00001), .t_string(chip_ID), .shift(block_paint_1_shift_2),
    .shift_2(block_paint_7_shift_2));  // open: t_string_2
  block_paint block_paint_8 (
    .data(register_4_q), .\string (5'b00010), .t_string(chip_ID), .shift(block_paint_1_shift_2));  // open: shift_2, t_string_2
  block_paint block_paint_9 (
    .data(register_5_q), .\string (5'b00100), .t_string(chip_ID), .shift(block_paint_3_shift_2),
    .shift_2(block_paint_9_shift_2));  // open: t_string_2
  block_paint block_paint_10 (
    .data(register_5_q), .\string (5'b00101), .t_string(chip_ID), .shift(block_paint_3_shift_2));  // open: shift_2, t_string_2
  block_paint block_paint_11 (
    .data(register_6_q), .\string (5'b00111), .t_string(chip_ID), .shift(block_paint_5_shift_2),
    .shift_2(block_paint_11_shift_2));  // open: t_string_2
  block_paint block_paint_12 (
    .data(register_6_q), .\string (5'b01000), .t_string(chip_ID), .shift(block_paint_5_shift_2));  // open: shift_2, t_string_2
  buf and_7 (and_7_out, min_comparator_7_result);  // AND_Gate
  min_comparator min_comparator_7 (
    .first(min_comparator_4_first_2), .second(min_comparator_4_second_2), .result(min_comparator_7_result),
    .second_2(min_comparator_7_second_2), .first_2(min_comparator_7_first_2));
  buf and_8 (and_8_out, min_comparator_8_result);  // AND_Gate
  min_comparator min_comparator_8 (
    .first(min_comparator_5_first_2), .second(min_comparator_5_second_2), .result(min_comparator_8_result),
    .second_2(min_comparator_8_second_2), .first_2(min_comparator_8_first_2));
  buf and_9 (and_9_out, min_comparator_9_result);  // AND_Gate
  min_comparator min_comparator_9 (
    .first(min_comparator_6_first_2), .second(min_comparator_6_second_2), .result(min_comparator_9_result),
    .second_2(min_comparator_9_second_2), .first_2(min_comparator_9_first_2));
  Register #(.width(5)) register_7 (.Q(register_7_q), .clr(and_7_out));  // open: D, en, clk
  Register #(.width(5)) register_8 (.Q(register_8_q), .clr(and_8_out));  // open: D, en, clk
  Register #(.width(5)) register_9 (.Q(register_9_q), .clr(and_9_out));  // open: D, en, clk
  block_paint block_paint_13 (
    .data(register_7_q), .\string (5'b00001), .t_string(chip_ID), .shift(block_paint_7_shift_2),
    .shift_2(block_paint_13_shift_2));  // open: t_string_2
  block_paint block_paint_14 (
    .data(register_7_q), .\string (5'b00010), .t_string(chip_ID), .shift(block_paint_7_shift_2));  // open: shift_2, t_string_2
  block_paint block_paint_15 (
    .data(register_8_q), .\string (5'b00100), .t_string(chip_ID), .shift(block_paint_9_shift_2),
    .shift_2(block_paint_15_shift_2));  // open: t_string_2
  block_paint block_paint_16 (
    .data(register_8_q), .\string (5'b00101), .t_string(chip_ID), .shift(block_paint_9_shift_2));  // open: shift_2, t_string_2
  block_paint block_paint_17 (
    .data(register_9_q), .\string (5'b00111), .t_string(chip_ID), .shift(block_paint_11_shift_2),
    .shift_2(block_paint_17_shift_2));  // open: t_string_2
  block_paint block_paint_18 (
    .data(register_9_q), .\string (5'b01000), .t_string(chip_ID), .shift(block_paint_11_shift_2));  // open: shift_2, t_string_2
  Register #(.width(5)) register_10 (.Q(register_10_q), .clr(and_10_out));  // open: D, en, clk
  buf and_10 (and_10_out, min_comparator_10_result);  // AND_Gate
  min_comparator min_comparator_10 (
    .first(min_comparator_7_first_2), .second(min_comparator_7_second_2), .result(min_comparator_10_result),
    .second_2(min_comparator_10_second_2), .first_2(min_comparator_10_first_2));
  Register #(.width(5)) register_11 (.Q(register_11_q), .clr(and_11_out));  // open: D, en, clk
  buf and_11 (and_11_out, min_comparator_11_result);  // AND_Gate
  min_comparator min_comparator_11 (
    .first(min_comparator_8_first_2), .second(min_comparator_8_second_2), .result(min_comparator_11_result),
    .second_2(min_comparator_11_second_2), .first_2(min_comparator_11_first_2));
  Register #(.width(5)) register_12 (.Q(register_12_q), .clr(and_12_out));  // open: D, en, clk
  buf and_12 (and_12_out, min_comparator_12_result);  // AND_Gate
  min_comparator min_comparator_12 (
    .first(min_comparator_9_first_2), .second(min_comparator_9_second_2), .result(min_comparator_12_result),
    .second_2(min_comparator_12_second_2), .first_2(min_comparator_12_first_2));
  block_paint block_paint_19 (
    .data(register_10_q), .\string (5'b00001), .t_string(chip_ID), .shift(block_paint_13_shift_2),
    .shift_2(block_paint_19_shift_2));  // open: t_string_2
  block_paint block_paint_20 (
    .data(register_10_q), .\string (5'b00010), .t_string(chip_ID), .shift(block_paint_13_shift_2));  // open: shift_2, t_string_2
  block_paint block_paint_21 (
    .data(register_11_q), .\string (5'b00100), .t_string(chip_ID), .shift(block_paint_15_shift_2),
    .shift_2(block_paint_21_shift_2));  // open: t_string_2
  block_paint block_paint_22 (
    .data(register_11_q), .\string (5'b00101), .t_string(chip_ID), .shift(block_paint_15_shift_2));  // open: shift_2, t_string_2
  block_paint block_paint_23 (
    .data(register_12_q), .\string (5'b00111), .t_string(chip_ID), .shift(block_paint_17_shift_2),
    .shift_2(block_paint_23_shift_2));  // open: t_string_2
  block_paint block_paint_24 (
    .data(register_12_q), .\string (5'b01000), .t_string(chip_ID), .shift(block_paint_17_shift_2));  // open: shift_2, t_string_2
  Register #(.width(5)) register_13 (.Q(register_13_q), .clr(and_13_out));  // open: D, en, clk
  buf and_13 (and_13_out, min_comparator_13_result);  // AND_Gate
  min_comparator min_comparator_13 (
    .first(min_comparator_10_first_2), .second(min_comparator_10_second_2),
    .result(min_comparator_13_result), .second_2(min_comparator_13_second_2),
    .first_2(min_comparator_13_first_2));
  Register #(.width(5)) register_14 (.Q(register_14_q), .clr(and_14_out));  // open: D, en, clk
  buf and_14 (and_14_out, min_comparator_14_result);  // AND_Gate
  min_comparator min_comparator_14 (
    .first(min_comparator_11_first_2), .second(min_comparator_11_second_2),
    .result(min_comparator_14_result), .second_2(min_comparator_14_second_2),
    .first_2(min_comparator_14_first_2));
  Register #(.width(5)) register_15 (.Q(register_15_q), .clr(and_15_out));  // open: D, en, clk
  buf and_15 (and_15_out, min_comparator_15_result);  // AND_Gate
  min_comparator min_comparator_15 (
    .first(min_comparator_12_first_2), .second(min_comparator_12_second_2),
    .result(min_comparator_15_result), .second_2(min_comparator_15_second_2),
    .first_2(min_comparator_15_first_2));
  block_paint block_paint_25 (
    .data(register_13_q), .\string (5'b00001), .t_string(chip_ID), .shift(block_paint_19_shift_2),
    .shift_2(block_paint_25_shift_2));  // open: t_string_2
  block_paint block_paint_26 (
    .data(register_13_q), .\string (5'b00010), .t_string(chip_ID), .shift(block_paint_19_shift_2));  // open: shift_2, t_string_2
  block_paint block_paint_27 (
    .data(register_14_q), .\string (5'b00100), .t_string(chip_ID), .shift(block_paint_21_shift_2),
    .shift_2(block_paint_27_shift_2));  // open: t_string_2
  block_paint block_paint_28 (
    .data(register_14_q), .\string (5'b00101), .t_string(chip_ID), .shift(block_paint_21_shift_2));  // open: shift_2, t_string_2
  block_paint block_paint_29 (
    .data(register_15_q), .\string (5'b00111), .t_string(chip_ID), .shift(block_paint_23_shift_2),
    .shift_2(block_paint_29_shift_2));  // open: t_string_2
  block_paint block_paint_30 (
    .data(register_15_q), .\string (5'b01000), .t_string(chip_ID), .shift(block_paint_23_shift_2));  // open: shift_2, t_string_2
  Register #(.width(5)) register_16 (.Q(register_16_q), .clr(and_16_out));  // open: D, en, clk
  buf and_16 (and_16_out, min_comparator_16_result);  // AND_Gate
  min_comparator min_comparator_16 (
    .first(min_comparator_13_first_2), .second(min_comparator_13_second_2),
    .result(min_comparator_16_result), .second_2(min_comparator_16_second_2),
    .first_2(min_comparator_16_first_2));
  Register #(.width(5)) register_17 (.Q(register_17_q), .clr(and_17_out));  // open: D, en, clk
  buf and_17 (and_17_out, min_comparator_17_result);  // AND_Gate
  min_comparator min_comparator_17 (
    .first(min_comparator_14_first_2), .second(min_comparator_14_second_2),
    .result(min_comparator_17_result), .second_2(min_comparator_17_second_2),
    .first_2(min_comparator_17_first_2));
  Register #(.width(5)) register_18 (.Q(register_18_q), .clr(and_18_out));  // open: D, en, clk
  buf and_18 (and_18_out, min_comparator_18_result);  // AND_Gate
  min_comparator min_comparator_18 (
    .first(min_comparator_15_first_2), .second(min_comparator_15_second_2),
    .result(min_comparator_18_result), .second_2(min_comparator_18_second_2),
    .first_2(min_comparator_18_first_2));
  block_paint block_paint_31 (
    .data(register_16_q), .\string (5'b00001), .t_string(chip_ID), .shift(block_paint_25_shift_2),
    .shift_2(block_paint_31_shift_2));  // open: t_string_2
  block_paint block_paint_32 (
    .data(register_16_q), .\string (5'b00010), .t_string(chip_ID), .shift(block_paint_25_shift_2));  // open: shift_2, t_string_2
  block_paint block_paint_33 (
    .data(register_17_q), .\string (5'b00100), .t_string(chip_ID), .shift(block_paint_27_shift_2),
    .shift_2(block_paint_33_shift_2));  // open: t_string_2
  block_paint block_paint_34 (
    .data(register_17_q), .\string (5'b00101), .t_string(chip_ID), .shift(block_paint_27_shift_2));  // open: shift_2, t_string_2
  block_paint block_paint_35 (
    .data(register_18_q), .\string (5'b00111), .t_string(chip_ID), .shift(block_paint_29_shift_2),
    .shift_2(block_paint_35_shift_2));  // open: t_string_2
  block_paint block_paint_36 (
    .data(register_18_q), .\string (5'b01000), .t_string(chip_ID), .shift(block_paint_29_shift_2));  // open: shift_2, t_string_2
  Register #(.width(5)) register_19 (.Q(register_19_q), .clr(and_19_out));  // open: D, en, clk
  buf and_19 (and_19_out, min_comparator_19_result);  // AND_Gate
  min_comparator min_comparator_19 (
    .first(min_comparator_16_first_2), .second(min_comparator_16_second_2),
    .result(min_comparator_19_result), .second_2(min_comparator_19_second_2),
    .first_2(min_comparator_19_first_2));
  Register #(.width(5)) register_20 (.Q(register_20_q), .clr(and_20_out));  // open: D, en, clk
  buf and_20 (and_20_out, min_comparator_20_result);  // AND_Gate
  min_comparator min_comparator_20 (
    .first(min_comparator_17_first_2), .second(min_comparator_17_second_2),
    .result(min_comparator_20_result), .second_2(min_comparator_20_second_2),
    .first_2(min_comparator_20_first_2));
  Register #(.width(5)) register_21 (.Q(register_21_q), .clr(and_21_out));  // open: D, en, clk
  buf and_21 (and_21_out, min_comparator_21_result);  // AND_Gate
  min_comparator min_comparator_21 (
    .first(min_comparator_18_first_2), .second(min_comparator_18_second_2),
    .result(min_comparator_21_result), .second_2(min_comparator_21_second_2),
    .first_2(min_comparator_21_first_2));
  block_paint block_paint_37 (
    .data(register_19_q), .\string (5'b00001), .t_string(chip_ID), .shift(block_paint_31_shift_2),
    .shift_2(block_paint_37_shift_2));  // open: t_string_2
  block_paint block_paint_38 (
    .data(register_19_q), .\string (5'b00010), .t_string(chip_ID), .shift(block_paint_31_shift_2));  // open: shift_2, t_string_2
  block_paint block_paint_39 (
    .data(register_20_q), .\string (5'b00100), .t_string(chip_ID), .shift(block_paint_33_shift_2),
    .shift_2(block_paint_39_shift_2));  // open: t_string_2
  block_paint block_paint_40 (
    .data(register_20_q), .\string (5'b00101), .t_string(chip_ID), .shift(block_paint_33_shift_2));  // open: shift_2, t_string_2
  block_paint block_paint_41 (
    .data(register_21_q), .\string (5'b00111), .t_string(chip_ID), .shift(block_paint_35_shift_2),
    .shift_2(block_paint_41_shift_2));  // open: t_string_2
  block_paint block_paint_42 (
    .data(register_21_q), .\string (5'b01000), .t_string(chip_ID), .shift(block_paint_35_shift_2));  // open: shift_2, t_string_2
  Register #(.width(5)) register_22 (.Q(register_22_q), .clr(and_22_out));  // open: D, en, clk
  buf and_22 (and_22_out, min_comparator_22_result);  // AND_Gate
  min_comparator min_comparator_22 (
    .first(min_comparator_19_first_2), .second(min_comparator_19_second_2), .result(min_comparator_22_result));  // open: second_2, first_2
  Register #(.width(5)) register_23 (.Q(register_23_q), .clr(and_23_out));  // open: D, en, clk
  buf and_23 (and_23_out, min_comparator_23_result);  // AND_Gate
  min_comparator min_comparator_23 (
    .first(min_comparator_20_first_2), .second(min_comparator_20_second_2), .result(min_comparator_23_result));  // open: second_2, first_2
  Register #(.width(5)) register_24 (.Q(register_24_q), .clr(and_24_out));  // open: D, en, clk
  buf and_24 (and_24_out, min_comparator_24_result);  // AND_Gate
  min_comparator min_comparator_24 (
    .first(min_comparator_21_first_2), .second(min_comparator_21_second_2), .result(min_comparator_24_result));  // open: second_2, first_2
  block_paint block_paint_43 (
    .data(register_22_q), .\string (5'b00001), .t_string(chip_ID), .shift(block_paint_37_shift_2));  // open: shift_2, t_string_2
  block_paint block_paint_44 (
    .data(register_22_q), .\string (5'b00010), .t_string(chip_ID), .shift(block_paint_37_shift_2));  // open: shift_2, t_string_2
  block_paint block_paint_45 (
    .data(register_23_q), .\string (5'b00100), .t_string(chip_ID), .shift(block_paint_39_shift_2));  // open: shift_2, t_string_2
  block_paint block_paint_46 (
    .data(register_23_q), .\string (5'b00101), .t_string(chip_ID), .shift(block_paint_39_shift_2));  // open: shift_2, t_string_2
  block_paint block_paint_47 (
    .data(register_24_q), .\string (5'b00111), .t_string(chip_ID), .shift(block_paint_41_shift_2));  // open: shift_2, t_string_2
  block_paint block_paint_48 (
    .data(register_24_q), .\string (5'b01000), .t_string(chip_ID), .shift(block_paint_41_shift_2));  // open: shift_2, t_string_2

  // Other names for the same wires on the sheet: chip[4:0] = chip_ID
endmodule

module block_paint (
  input  [4:0] data,
  input  [4:0] \string ,
  input  [4:0] t_string,
  input  [4:0] shift,
  output [31:0] t_string_2,
  output [4:0] shift_2
);

  wire comparator_1_eq;
  wire [31:0] decoder_32_inv_1_out, multiplexer_1_out, shifter_1_out, shifter_2_out, shifter_3_out;

  Comparator #(.width(5)) comparator_1 (.a(data), .b({5{1'b0}}), .eq(comparator_1_eq));  // open: gt, lt
  decoder_32_inv decoder_32_inv_1 (.data(data), .A(\string ), .B(t_string), .out(decoder_32_inv_1_out));
  Shifter #(.width(32), .shift("lr")) shifter_1 (.in(decoder_32_inv_1_out), .\dist (shift), .out(shifter_1_out));
  Adder #(.width(5)) adder_1 (.a(shift), .b(5'b00100), .out(shift_2));  // open: cin, cout
  Multiplexer #(.width(32)) multiplexer_1 (
    .in0(shifter_1_out), .in1({32{1'b0}}), .out(multiplexer_1_out), .sel(1'b1), .en(comparator_1_eq));
  Shifter #(.width(32)) shifter_2 (.in(multiplexer_1_out), .\dist (5'b00010), .out(shifter_2_out));
  Shifter #(.width(32)) shifter_3 (.in(multiplexer_1_out), .\dist (5'b00001), .out(shifter_3_out));
  assign t_string_2 = multiplexer_1_out | shifter_2_out | shifter_3_out;  // OR_Gate or_1, 32 bits wide
endmodule

module min_comparator (
  input  [4:0] first,
  input  [4:0] second,
  output [4:0] first_2,
  output result,
  output [4:0] second_2
);

  Comparator #(.width(5)) comparator_1 (.a(first), .b(second), .eq(result));  // open: gt, lt
  Adder #(.width(5)) adder_1 (.a(second), .b(5'b00001), .out(second_2));  // open: cin, cout

  assign first_2 = first;
endmodule
